# Fritzing sketch Huzzah-motor (saved by Fritzing 0.9.3b)
breadboards: 1

parts:
  Part1 = Adafruit Feather HUZZAH ESP8266 [part_number="Adafruit #2821"]
  Battery = 4xAA Switchable Battery Pack w/JST connector
  diode = P1000K [part_number=P1000K]
  DC_Motor = DC Motor
  R1 = Resistor [tolerance=±5% resistance=10k package="2010 [SMD]"]
  Capacitor = Electrolytic Capacitor [capacitance=100μF package="0807 [SMD, electrolytic]"]
  Button = Momentary Switch [package=ksa_sealed_tac_switch]
  MOSFET = Basic FET N-Channel [package="TO220 [THT]"]
  J1 = Basic Servo

nets (from the schematic view):
  N1: Part1.GPIO13/MOSI, Button.2
  GND: Part1.GND, Battery.NEG, R1.Pin_1, Capacitor.-, MOSFET.source, J1.gnd
  N2: Part1.3.3V, Button.4
  N3: Part1.GPIO12/MISO, J1.pulse
  N4: Part1.GPIO15, R1.Pin_0, MOSFET.gate
  N5: Battery.POS, diode.cathode, DC_Motor.pin_2, Capacitor.+, J1.vcc
  N6: diode.anode, DC_Motor.pin_1, MOSFET.drain

notes:
  GPIO13/button: interne pull-up
  Let op: 5V power rail
  <-- Let op: 3.3V power rail
  Als externe batterij is aangesloten op Huzzah, dan BAT-pin verbinden met de bovenste rode breadboard-lijn (5V)

custom parts:
  Adafruit Feather HUZZAH ESP8266: his is the Adafruit Feather HUZZAH ESP8266 - our take on an 'all-in-one' ESP8266 WiFi development board with built in USB and battery charging. Its an ESP8266 WiFi module with all the extras you need, ready to rock! We have other boards in the Feather family, check'em out here. At the Feather HUZZAH's heart is an ESP8266 WiFi microcontroller clocked at 80 MHz and at 3.3V logic. This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
  4xAA Switchable Battery Pack w/JST connector: 4xAA Switchable Battery Pack with JST connector
